// Logisim project z8ProcessorSchematic.circ as structural Verilog: 5 circuits, main circuit main
module main (
);

  ALU alu_1 ();  // open: in_a, in_b, enable, alu_op, out_5, alu_out
endmodule

module ALU_op_sel (
  input  enable,
  input  [2:0] op,
  output alu_add,
  output alu_sub,
  output alu_inc,
  output alu_dec,
  output alu_and,
  output alu_or,
  output alu_xor,
  output alu_comp
);

  Decoder #(.select(3)) decoder_1 (
    .out0(alu_add), .out1(alu_sub), .out2(alu_inc), .out3(alu_dec), .out4(alu_and), .out5(alu_or),
    .out6(alu_xor), .out7(alu_comp), .sel(op), .en(enable));
endmodule

module ALU (
  input  [7:0] in_a,
  input  [7:0] in_b,
  input  enable,
  input  [2:0] alu_op,
  output [3:0] out_5,
  output [7:0] alu_out
);

  wire alu_op_sel_1_alu_add, alu_op_sel_1_alu_sub;
  wire [3:0] alu_add_1_add_flags_out, alu_sub_1_sub_flags_out, bit_extender_1_out, multiplexer_1_out;
  wire [7:0] alu_add_1_add_out, alu_sub_1_sub_out, bit_extender_2_out, multiplexer_2_out;

  ALU_op_sel alu_op_sel_1 (
    .enable(enable), .op(alu_op), .alu_add(alu_op_sel_1_alu_add), .alu_sub(alu_op_sel_1_alu_sub));  // open: alu_inc, alu_dec, alu_and, alu_or, alu_xor, alu_comp
  ALU_add alu_add_1 (
    .enable(alu_op_sel_1_alu_add), .in_a(in_a), .in_b(in_b), .add_out(alu_add_1_add_out),
    .add_flags_out(alu_add_1_add_flags_out));
  ALU_sub alu_sub_1 (
    .enable(alu_op_sel_1_alu_sub), .in_a(in_a), .in_b(in_b), .sub_out(alu_sub_1_sub_out),
    .sub_flags_out(alu_sub_1_sub_flags_out));
  Multiplexer #(.select(3), .width(4)) multiplexer_1 (
    .in0(alu_add_1_add_flags_out), .in1(alu_sub_1_sub_flags_out), .out(multiplexer_1_out), .sel(alu_op));  // open: in2, in3, in4, in5, in6, in7
  Multiplexer #(.select(3), .width(8)) multiplexer_2 (
    .in0(alu_add_1_add_out), .in1(alu_sub_1_sub_out), .out(multiplexer_2_out), .sel(alu_op));  // open: in2, in3, in4, in5, in6, in7
  assign bit_extender_1_out = {{3{enable}}, enable};  // Bit_Extender bit_extender_1
  assign bit_extender_2_out = {{7{enable}}, enable};  // Bit_Extender bit_extender_2
  assign out_5 = multiplexer_1_out & bit_extender_1_out;  // AND_Gate and_1, 4 bits wide
  assign alu_out = multiplexer_2_out & bit_extender_2_out;  // AND_Gate and_2, 8 bits wide
endmodule

module ALU_add (
  input  enable,
  input  [7:0] in_a,
  input  [7:0] in_b,
  output [7:0] add_out,
  output [3:0] add_flags_out
);

  wire not_1_out, xor_1_out, xor_2_out, zero_flag_out;
  wire [3:0] not_2_out;
  wire [7:0] adder_1_out, bit_extender_1_out;

  assign bit_extender_1_out = {{7{enable}}, enable};  // Bit_Extender bit_extender_1
  Adder adder_1 (.a(in_a), .b(in_b), .out(adder_1_out), .cout(not_2_out[2]));  // open: cin
  assign add_out = bit_extender_1_out & adder_1_out;  // AND_Gate and_1, 8 bits wide
  xor xor_1 (xor_1_out, in_a[7], in_b[7]);
  not not_1 (not_1_out, xor_1_out);
  or zero_flag (zero_flag_out, add_out[0], add_out[1], add_out[2], add_out[3], add_out[4], add_out[5], add_out[6], add_out[7]);
  xor xor_2 (xor_2_out, add_out[7], in_a[7]);
  not not_2 (not_2_out[0], zero_flag_out);
  and and_2 (not_2_out[3], xor_2_out, not_1_out);
  assign add_flags_out = bit_extender_1_out[7:4] & {not_2_out[3:2], add_out[7], not_2_out[0]};  // AND_Gate and_3, 4 bits wide
endmodule

module ALU_sub (
  input  enable,
  input  [7:0] in_a,
  input  [7:0] in_b,
  output [7:0] sub_out,
  output [3:0] sub_flags_out
);

  wire not_2_out, or_1_out, xor_1_out, xor_2_out;
  wire [6:0] subtractor_1_out;
  wire [7:0] bit_extender_1_out;

  assign bit_extender_1_out = {{7{enable}}, enable};  // Bit_Extender bit_extender_1
  Subtractor subtractor_1 (
    .a(in_a), .b(in_b), .out({sub_flags_out[1], subtractor_1_out}), .bout(sub_flags_out[2]));  // open: bin
  xor xor_1 (xor_1_out, in_a[7], in_b[7]);
  assign sub_out = bit_extender_1_out & {sub_flags_out[1], subtractor_1_out};  // AND_Gate and_1, 8 bits wide
  xor xor_2 (xor_2_out, sub_flags_out[1], in_b[7]);
  or or_1 (or_1_out, subtractor_1_out[0], subtractor_1_out[1], subtractor_1_out[2], subtractor_1_out[3], subtractor_1_out[4], subtractor_1_out[5], subtractor_1_out[6], sub_flags_out[1]);
  not not_1 (sub_flags_out[0], or_1_out);
  not not_2 (not_2_out, xor_2_out);
  and and_2 (sub_flags_out[3], not_2_out, xor_1_out);
endmodule
